# Fritzing sketch Angle leg detection (saved by Fritzing 0.9.10b)
breadboards: 1

parts:
  Part1 = Adafruit Feather nRF52 [part_number="Adafruit #3406"]
  Part2 = Adafruit ADXL335 [part_number="Adafruit #163"]

nets:
  3.3V: Part1.3.3V, Part2.VIN
  GND: Part1.GND, Part2.GND
  N1: Part1.A1/0.03, Part2.ZOUT
  N2: Part1.A2/0.04, Part2.YOUT
  N3: Part1.A3/0.05, Part2.XOUT

custom parts:
  Adafruit ADXL335: We've updated our favorite triple-axis accelerometer to now have an on-board 3.3V regulator - making it a perfect choice for interfacing with a 5V microcontroller such as the Arduino. This breakout comes with 3 analog outputs for X, Y and Z axis measurements on a 0.75"x0.75" breakout board. The ADXL335 is the latest and greatest from Analog Devices, known for their exceptional quality MEMS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
