# Fritzing sketch Basic Sketch (saved by Fritzing 0.9.10b)

parts:
  Part1 = Arduino Uno (Rev3)
  LED1 = RGB LED (com. anode, rbg) [package="5 mm [THT]"]
  M1 = Dagu DGServo 9g (Pan and tilt) [part_number=RS001B]
  S1 = Pushbutton [package="[THT]"]
  S2 = Pushbutton [package="[THT]"]
  R1 = Resistor [tolerance=±5% resistance=10 package="2010 [SMD]"]
  R2 = Resistor [tolerance=±5% resistance=10 package="2010 [SMD]"]
  S3 = Pushbutton [package="[THT]"]
  R3 = Resistor [tolerance=±5% resistance=10 package="2010 [SMD]"]

nets:
  N1: Part1.D8, LED1.green_cathode
  N2: Part1.D9_PWM, M1.pulse
  N3: Part1.D12/MISO, LED1.blue_cathode
  N4: Part1.D13/SCK, LED1.red_cathode
  GND: Part1.GND, LED1.common_anode, M1.gnd, R1.Pin_1, R2.Pin_1, R3.Pin_1
  N5: Part1.D2, S1.Pin_3, S1.Pin_4, R1.Pin_0
  N6: Part1.D4, S2.Pin_3, S2.Pin_4, R2.Pin_0
  N7: Part1.D7, S3.Pin_3, S3.Pin_4, R3.Pin_0
  5V: Part1.5V, M1.vcc, S1.Pin_1, S1.Pin_2, S2.Pin_1, S2.Pin_2, S3.Pin_1, S3.Pin_2

// code stored in the sketch: Script.ino
// C++ Code
//
#include <Servo.h>
Servo motor;
int position = 0;

// Button
const int BUTTON1 = 2;
const int BUTTON2 = 4;
const int BUTTON3 = 7;

// LED
const int RED = 13;
const int BLUE = 12;
const int GREEN = 8;

// Button State
int buttonState1 = 0;
int buttonState2 = 0;
int buttonState3 = 0;

void setup() {
  // put your setup code here, to run once:
  pinMode(BUTTON1, INPUT);
  pinMode(BUTTON2, INPUT);
  pinMode(BUTTON3, INPUT);

  // OUTPUT
  pinMode(RED, OUTPUT);
  pinMode(GREEN, OUTPUT);
  pinMode(BLUE, OUTPUT);

  // SERVO
  motor.attach(9);
  motor.write(0);

  // Initial Light Check
  digitalWrite(RED, HIGH);
  delay(500);
  digitalWrite(RED, LOW);
  digitalWrite(BLUE, HIGH);
  delay(500);
  digitalWrite(BLUE, LOW);
  digitalWrite(GREEN,HIGH);
  delay(500);
  digitalWrite(GREEN,LOW);

  Serial.begin(9600);
}

void loop() {
  // put your main code here, to run repeatedly:
  buttonState1 = digitalRead(BUTTON1);
  if(buttonState1 == HIGH) {
    digitalWrite(RED, HIGH);
    motor.write(0);
  }
  else {
    digitalWrite(RED, LOW);
  }
  
  buttonState2 = digitalRead(BUTTON2);
  if(buttonState2 == HIGH) {
    digitalWrite(BLUE, HIGH);
    motor.write(90);
  }
  else {
    digitalWrite(BLUE, LOW);
  }
  
  buttonState3 = digitalRead(BUTTON3);
  if(buttonState3 == HIGH) {
    digitalWrite(GREEN, HIGH);
    motor.write(140);
  }
  else {
    digitalWrite(GREEN,LOW);
  }
}
